# Fritzing sketch Cava (saved by Fritzing 0.9.3b)
breadboards: 1

parts:
  S1 = Momentary Switch [package=ksa_sealed_tac_switch]
  S2 = Momentary Switch [package=ksa_sealed_tac_switch]
  U1 = 7-SEGMENT-DISPLAY [package=7-segment-display]  # not connected
  U2 = 7-SEGMENT-DISPLAY [package=7-segment-display]  # not connected
  U3 = SN74LS47N [package="DIP16 [THT]"]
  U4 = SN74LS47N [package="DIP16 [THT]"]
  Componente1 = Arduino Uno (Rev3)  # not connected
  J1 = Peltier Element  # not connected
  IC1 = L293D [package=THT]
  U5 = TMP102 [package=sot563]

nets:
  GND: S1.4, S2.4, U3.GND, U4.GND, IC1.0V, U5.GND
  VCC: U3.VCC, U4.VCC, IC1.+V, U5.ADD0, U5.VCC

custom parts:
  SN74LS47N: BCD-TO-SEVEN-SEGMENT DECODERS/DRIVRES
